# Fritzing sketch fritzing_wiringdiagram (saved by Fritzing 0.9.2b)

parts:
  Part1 = Arduino Uno (Rev3)
  U1 = HIH-4030 [package=hih-4030]

nets:
  N1: Part1.A0, U1.OUT
  5V: Part1.5V, U1.VCC
  GND: Part1.GND, U1.GND

notes:
  Tinkur Bootdryer
  www.tinkurlab.com
